# Fritzing sketch openPFGE H1.1 (saved by Fritzing 0.9.3b)
circuit board: 10cm x 5cm
breadboards: 1

parts:
  HC05 = Bluetooth HC-05 Macho
  LCD = Header 4 [package=molex-1x4_lock]
  7805 = Voltage Regulator [package=to220-igo]
  10K = Resistor [tolerance=±5% resistance=220 package=THT]
  Arduino_Nano = Arduino Nano (Rev3.0)
  Thermo = Screw terminal - 2 pins [package=THT]
  12V = Screw terminal - 2 pins [package=THT]
  Switch = Screw terminal - 2 pins [package=THT]
  Servo = screw terminal, 3 pins
  Fan_1 = Screw terminal - 2 pins [package=THT]
  Fan_2 = Screw terminal - 2 pins [package=THT]
  IRF740 = Basic FET N-Channel [package="TO220 [THT]"]
  IRF741 = Basic FET N-Channel [package="TO220 [THT]"]

nets:
  N1: HC05.TXD, Arduino_Nano.D10
  N2: HC05.RXD, Arduino_Nano.D11/MOSI
  VCC: HC05.VCC, LCD.2, 7805.OUT, Arduino_Nano.5V, Servo.pin2
  GND: HC05.GND, LCD.1, 7805.GND, Arduino_Nano.GND, Thermo.pin1, 12V.pin1, Servo.pin1, IRF740.source, IRF741.source
  N3: LCD.3, Arduino_Nano.A4
  N4: LCD.4, Arduino_Nano.A5
  N5: 7805.IN, Switch.pin2
  N6: 10K.Pin_0, Arduino_Nano.AREF, Arduino_Nano.3V3
  N7: 10K.Pin_1, Arduino_Nano.A0, Thermo.pin2
  N8: Arduino_Nano.D5, IRF741.gate
  N9: Arduino_Nano.D6, IRF740.gate
  N10: Arduino_Nano.D9, Servo.pin3
  N11: 12V.pin2, Switch.pin1
  N12: Fan_1.pin1, IRF741.drain
  N13: Fan_2.pin1, IRF740.drain

notes:
  +
