# Fritzing sketch openPFGE H1.2 (saved by Fritzing 0.9.3b)
circuit board: 10cm x 5.05cm
breadboards: 1

parts:
  HC05 = Bluetooth HC-05 Macho
  LCD/OLED = Header 4 [package=molex-1x4_lock]
  7805 = Voltage Regulator [package=to220-igo]
  10K = Resistor [tolerance=±5% resistance=10k package=THT]
  Arduino_Nano = Arduino Nano (Rev3.0)
  Thermo = Screw terminal - 2 pins [package=THT]
  12V = Screw terminal - 2 pins [package=THT]
  Switch = Screw terminal - 2 pins [package=THT]
  Servo = screw terminal, 3 pins
  Fan_1 = Screw terminal - 2 pins [package=THT]
  Mosfet = Basic FET N-Channel [package="TO220 [THT]"]
  Mosfet_2 = Basic FET N-Channel [package="TO220 [THT]"]
  10K_2 = Resistor [tolerance=±5% resistance=10k package=THT]
  10K_3 = Resistor [tolerance=±5% resistance=10k package=THT]
  Pelt1 = Screw terminal - 2 pins [package=THT]
  Pelt2 = Screw terminal - 2 pins [package=THT]
  Mosfet_3 = Basic FET N-Channel [package="TO220 [THT]"]
  Mosfet_4 = Basic FET N-Channel [package="TO220 [THT]"]
  10K_4 = Resistor [tolerance=±5% resistance=10k package=THT]
  10K_5 = Resistor [tolerance=±5% resistance=10k package=THT]
  Diode = Rectifier Diode [part_number=1N4001 package="300 mil [THT]"]
  Fan_2 = Screw terminal - 2 pins [package=THT]
  Pump = Screw terminal - 2 pins [package=THT]
  Mosfet_5 = Basic FET N-Channel [package="TO220 [THT]"]
  Diode_2 = Rectifier Diode [part_number=1N4001 package="300 mil [THT]"]
  10K_6 = Resistor [tolerance=±5% resistance=10k package=THT]
  10uF = Electrolytic Capacitor [capacitance=10µF package="100 mil [THT, electrolytic]"]
  100uF = Electrolytic Capacitor [capacitance=100µF package="100 mil [THT, electrolytic]"]
  Diode1 = Rectifier Diode [part_number=1N4001 package="300 mil [THT]"]

nets:
  N1: HC05.TXD, Arduino_Nano.D10
  N2: HC05.RXD, Arduino_Nano.D11/MOSI
  VCC: HC05.VCC, LCD/OLED.2, 7805.OUT, Arduino_Nano.5V, Servo.pin2, 10uF.+
  GND: HC05.GND, LCD/OLED.1, 7805.GND, Arduino_Nano.GND, Thermo.pin1, 12V.pin1, Servo.pin1, Mosfet.source, Mosfet_2.source, 10K_2.Pin_1, 10K_3.Pin_1, Mosfet_3.source, Mosfet_4.source, 10K_4.Pin_1, 10K_5.Pin_1, Mosfet_5.source, 10K_6.Pin_0, 10uF.-, 100uF.-
  N3: LCD/OLED.3, Arduino_Nano.A4
  N4: LCD/OLED.4, Arduino_Nano.A5
  N5: 7805.IN, Arduino_Nano.VIN, Switch.pin2, Fan_1.pin2, Pelt1.pin2, Pelt2.pin2, Diode.cathode, Fan_2.pin2, Pump.pin2, Diode_2.cathode, 100uF.+, Diode1.cathode
  N6: 10K.Pin_0, Arduino_Nano.AREF, Arduino_Nano.3V3
  N7: 10K.Pin_1, Arduino_Nano.A0, Thermo.pin2
  N8: Arduino_Nano.D4, Mosfet_5.gate, 10K_6.Pin_1
  N9: Arduino_Nano.D5, Mosfet_2.gate, 10K_2.Pin_0
  N10: Arduino_Nano.D6, Mosfet.gate, 10K_3.Pin_0
  N11: Arduino_Nano.D7, Mosfet_4.gate, 10K_5.Pin_0
  N12: Arduino_Nano.D8, Mosfet_3.gate, 10K_4.Pin_0
  N13: Arduino_Nano.D9, Servo.pin3
  N14: 12V.pin2, Switch.pin1
  N15: Fan_1.pin1, Mosfet_2.drain, Diode.anode
  N16: Mosfet.drain, Fan_2.pin1, Diode1.anode
  N17: Pelt1.pin1, Mosfet_3.drain
  N18: Pelt2.pin1, Mosfet_4.drain
  N19: Pump.pin1, Mosfet_5.drain, Diode_2.anode

notes:
  +
  H1.2
  -
  +12V
  In
  +5V
  D9
  A0
  3.3V
  RX-D11
  SDA-A4
  SCL-A5
  TX-D10
  C  D  S
  D8
  D7
  D6
  D5
  D4
  IN
  OUT
